// Logisim project alu.circ as structural Verilog: 1 circuit, main circuit alu
module alu (
  input  [31:0] A,
  input  [31:0] B,
  input  [3:0] ALUSel,
  output [31:0] Result
);

  wire comparator_1_lt;
  wire [4:0] bit_extender_1_out, bit_extender_2_out, bit_extender_3_out;
  wire [31:0] add0, and7, mul8, mulh9, mulhu11, multiplexer_1_out, multiplexer_2_out, multiplexer_3_out,
       multiplexer_4_out, multiplexer_5_out, multiplexer_6_out, multiplexer_7_out, multiplexer_8_out,
       multiplexer_9_out, multiplexer_10_out, multiplexer_11_out, multiplexer_12_out, multiplexer_13_out,
       multiplexer_14_out, or6, sll1, slt2, sra13, srl5, sub12, xor4;

  Comparator #(.width(32)) comparator_1 (.a(A), .b(B), .lt(comparator_1_lt));  // open: gt, eq
  Adder #(.width(32)) adder_1 (.a(A), .b(B), .out(add0));  // open: cin, cout
  Shifter #(.width(32)) shifter_1 (.in(A), .\dist (bit_extender_1_out), .out(sll1));
  Bit_Extender #(.in_width(32), .out_width(5)) bit_extender_1 (.in(B), .out(bit_extender_1_out));
  Shifter #(.shift("lr"), .width(32)) shifter_2 (.in(A), .\dist (bit_extender_2_out), .out(srl5));
  Bit_Extender #(.in_width(32), .out_width(5)) bit_extender_2 (.in(B), .out(bit_extender_2_out));
  Shifter #(.shift("ar"), .width(32)) shifter_3 (.in(A), .\dist (bit_extender_3_out), .out(sra13));
  Bit_Extender #(.in_width(32), .out_width(5)) bit_extender_3 (.in(B), .out(bit_extender_3_out));
  assign xor4 = A ^ B;  // XOR_Gate xor_1, 32 bits wide
  assign or6 = A | B;  // OR_Gate or_1, 32 bits wide
  assign and7 = A & B;  // AND_Gate and_1, 32 bits wide
  Multiplier #(.mode("twosComplement"), .width(32)) multiplier_1 (.a(A), .b(B), .out(mul8), .cout(mulh9));  // open: cin
  Multiplier #(.width(32)) multiplier_2 (.a(A), .b(B), .cout(mulhu11));  // open: out, cin
  Subtractor #(.width(32)) subtractor_1 (.a(A), .b(B), .out(sub12));  // open: bin, bout
  assign slt2 = {{31{1'b0}}, comparator_1_lt};  // Bit_Extender bit_extender_4
  Multiplexer #(.enable("false"), .width(32)) multiplexer_1 (
    .in0(add0), .in1(sll1), .out(multiplexer_1_out), .sel(ALUSel[0]));
  Multiplexer #(.enable("false"), .width(32)) multiplexer_2 (
    .in0(slt2), .out(multiplexer_2_out), .sel(ALUSel[0]));  // open: in1
  Multiplexer #(.enable("false"), .width(32)) multiplexer_3 (
    .in0(xor4), .in1(srl5), .out(multiplexer_3_out), .sel(ALUSel[0]));
  Multiplexer #(.enable("false"), .width(32)) multiplexer_4 (
    .in0(or6), .in1(and7), .out(multiplexer_4_out), .sel(ALUSel[0]));
  Multiplexer #(.enable("false"), .width(32)) multiplexer_5 (
    .in0(mul8), .in1(mulh9), .out(multiplexer_5_out), .sel(ALUSel[0]));
  Multiplexer #(.enable("false"), .width(32)) multiplexer_6 (
    .in1(mulhu11), .out(multiplexer_6_out), .sel(ALUSel[0]));  // open: in0
  Multiplexer #(.enable("false"), .width(32)) multiplexer_7 (
    .in0(sub12), .in1(sra13), .out(multiplexer_7_out), .sel(ALUSel[0]));
  Multiplexer #(.enable("false"), .width(32)) multiplexer_8 (
    .in1(B), .out(multiplexer_8_out), .sel(ALUSel[0]));  // open: in0
  Multiplexer #(.enable("false"), .width(32)) multiplexer_9 (
    .in0(multiplexer_1_out), .in1(multiplexer_2_out), .out(multiplexer_9_out), .sel(ALUSel[1]));
  Multiplexer #(.enable("false"), .width(32)) multiplexer_10 (
    .in0(multiplexer_3_out), .in1(multiplexer_4_out), .out(multiplexer_10_out), .sel(ALUSel[1]));
  Multiplexer #(.enable("false"), .width(32)) multiplexer_11 (
    .in0(multiplexer_5_out), .in1(multiplexer_6_out), .out(multiplexer_11_out), .sel(ALUSel[1]));
  Multiplexer #(.enable("false"), .width(32)) multiplexer_12 (
    .in0(multiplexer_7_out), .in1(multiplexer_8_out), .out(multiplexer_12_out), .sel(ALUSel[1]));
  Multiplexer #(.enable("false"), .width(32)) multiplexer_13 (
    .in0(multiplexer_9_out), .in1(multiplexer_10_out), .out(multiplexer_13_out), .sel(ALUSel[2]));
  Multiplexer #(.enable("false"), .width(32)) multiplexer_14 (
    .in0(multiplexer_11_out), .in1(multiplexer_12_out), .out(multiplexer_14_out), .sel(ALUSel[2]));
  Multiplexer #(.enable("false"), .width(32)) multiplexer_15 (
    .in0(multiplexer_13_out), .in1(multiplexer_14_out), .out(Result), .sel(ALUSel[3]));

  // Other names for the same wires on the sheet: s0 = ALUSel[0]; s1 = ALUSel[1]; s2 = ALUSel[2]; s3 = ALUSel[3];
  //   bsel15[31:0] = B

  // Notes on the sheet:
  //   INPUTS to your circuit
  //   DON'T CHANGE THE LOCATIONS OF THE INPUTS AND OUTPUTS!
  //   OUTPUT from your circuit
endmodule
