// Logisim project cpu.circ as structural Verilog: 1 circuit, main circuit cpu
module cpu (
  input  clk,
  input  [31:0] INSTRUCTION,
  input  [31:0] MEM_READ_DATA,
  output [31:0] MEM_WRITE_ADDRESS,
  output [31:0] PROGRAM_COUNTER,
  output [31:0] ra,
  output [31:0] sp,
  output [31:0] t0,
  output [31:0] t1,
  output [31:0] t2,
  output [31:0] s0,
  output [31:0] s1,
  output [31:0] a0,
  output [31:0] tohost,
  output [3:0] MEM_WRITE_ENABLE,
  output [31:0] MEM_WRITE_DATA
);

  wire and_1_out, and_2_out, and_3_out, and_4_out, and_5_out, and_6_out, and_7_out, branch_comp_1_breq,
       branch_comp_1_brlt, comparator_1_eq, comparator_2_eq, comparator_3_eq, comparator_4_eq,
       comparator_5_eq, comparator_6_eq, comparator_7_eq, control_logic_1_asel, control_logic_1_brun,
       control_logic_1_bsel, control_logic_1_csrsel, control_logic_1_csrwen, control_logic_1_memrw,
       control_logic_1_pcsel, control_logic_1_regwen, not_1_out, not_2_out;
  wire [1:0] control_logic_1_wbsel, priority_encoder_2_out;
  wire [2:0] control_logic_1_immsel, funct3;
  wire [3:0] control_logic_1_alusel, priority_encoder_1_out;
  wire [7:0] multiplexer_7_out, multiplexer_8_out, multiplexer_10_out, multiplexer_15_out,
       multiplexer_16_out, multiplexer_17_out, multiplexer_18_out, multiplexer_19_out, multiplexer_20_out,
       multiplexer_21_out, multiplexer_22_out, regfile_1_read_data_2, regfile_1_read_data_2_2,
       regfile_1_read_data_2_3, regfile_1_read_data_2_4;
  wire [11:0] csrr;
  wire [15:0] multiplexer_9_out;
  wire [19:0] ins;
  wire [31:0] adder_1_out, bit_extender_1_out, bit_extender_2_out, counter, imm, multiplexer_1_out,
       multiplexer_2_out, multiplexer_3_out, multiplexer_4_out, multiplexer_5_out, multiplexer_6_out,
       multiplexer_11_out, multiplexer_14_out, read, regfile_1_read_data_1;

  Adder #(.width(32)) adder_1 (.a(PROGRAM_COUNTER), .b(32'h4), .out(adder_1_out));  // open: cin, cout
  Multiplexer #(.enable("false"), .width(32)) multiplexer_1 (
    .in0(INSTRUCTION), .in1(32'h13), .out(multiplexer_1_out), .sel(control_logic_1_pcsel));
  Multiplexer #(.enable("false"), .width(32)) multiplexer_2 (
    .in0(adder_1_out), .in1(MEM_WRITE_ADDRESS), .out(multiplexer_2_out), .sel(control_logic_1_pcsel));
  Register #(.width(32)) PC (.D(multiplexer_2_out), .clk(clk), .Q(PROGRAM_COUNTER));  // open: en, clr
  Register #(.width(32)) register_1 (
    .D(multiplexer_1_out), .clk(clk), .Q({csrr, ins[19:15], funct3, ins[11:0]}));  // open: en, clr
  Register #(.width(32)) register_2 (.D(PROGRAM_COUNTER), .clk(clk), .Q(counter));  // open: en, clr
  imm_gen imm_gen_1 (.inst({csrr, ins[19:15], funct3, ins[11:0]}), .ImmSel(control_logic_1_immsel), .imm(imm));
  control_logic control_logic_1 (
    .CSRWen(control_logic_1_csrwen), .PCSel(control_logic_1_pcsel), .RegWEn(control_logic_1_regwen),
    .ImmSel(control_logic_1_immsel), .BrUn(control_logic_1_brun), .ASel(control_logic_1_asel),
    .BSel(control_logic_1_bsel), .ALUSel(control_logic_1_alusel), .MemRW(control_logic_1_memrw),
    .WBSel(control_logic_1_wbsel), .CSRSel(control_logic_1_csrsel),
    .inst({csrr, ins[19:15], funct3, ins[11:0]}), .BrEq(branch_comp_1_breq), .BrLt(branch_comp_1_brlt));
  Multiplexer #(.enable("false"), .select(2), .width(32)) multiplexer_3 (
    .in0(read), .in1(MEM_WRITE_ADDRESS), .in2(adder_1_out), .out(multiplexer_3_out),
    .sel(control_logic_1_wbsel));  // open: in3
  regfile regfile_1 (
    .rs1(ins[19:15]), .rs2(csrr[4:0]), .rd(ins[11:7]), .Write_Data(multiplexer_3_out),
    .RegWEn(control_logic_1_regwen), .clk(clk), .ra(ra), .sp(sp), .t0(t0), .t1(t1), .t2(t2), .s0(s0),
    .s1(s1), .a0(a0), .Read_Data_1(regfile_1_read_data_1),
    .Read_Data_2({regfile_1_read_data_2_4, regfile_1_read_data_2_3, regfile_1_read_data_2_2, regfile_1_read_data_2}));
  branch_comp branch_comp_1 (
    .rs1(regfile_1_read_data_1),
    .rs2({regfile_1_read_data_2_4, regfile_1_read_data_2_3, regfile_1_read_data_2_2, regfile_1_read_data_2}),
    .BrUn(control_logic_1_brun), .BrEq(branch_comp_1_breq), .BrLt(branch_comp_1_brlt));
  Multiplexer #(.enable("false"), .width(32)) multiplexer_4 (
    .in0(regfile_1_read_data_1), .in1(counter), .out(multiplexer_4_out), .sel(control_logic_1_asel));
  Multiplexer #(.enable("false"), .width(32)) multiplexer_5 (
    .in0({regfile_1_read_data_2_4, regfile_1_read_data_2_3, regfile_1_read_data_2_2, regfile_1_read_data_2}),
    .in1(imm), .out(multiplexer_5_out), .sel(control_logic_1_bsel));
  Multiplexer #(.enable("false"), .width(32)) multiplexer_6 (
    .in0(regfile_1_read_data_1), .in1(imm), .out(multiplexer_6_out), .sel(control_logic_1_csrsel));
  alu alu_1 (.Result(MEM_WRITE_ADDRESS), .A(multiplexer_4_out), .B(multiplexer_5_out), .ALUSel(control_logic_1_alusel));
  // csr csr_1: pin names not known; wires that end beside it: csrr, multiplexer_6_out, control_logic_1_csrwen, clk, tohost
  Multiplexer #(.enable("false"), .width(8)) multiplexer_7 (
    .in0(MEM_READ_DATA[7:0]), .in1(MEM_READ_DATA[15:8]), .out(multiplexer_7_out), .sel(MEM_WRITE_ADDRESS[0]));
  Multiplexer #(.enable("false"), .width(8)) multiplexer_8 (
    .in0(MEM_READ_DATA[23:16]), .in1(MEM_READ_DATA[31:24]), .out(multiplexer_8_out),
    .sel(MEM_WRITE_ADDRESS[0]));
  Multiplexer #(.enable("false"), .width(16)) multiplexer_9 (
    .in0(MEM_READ_DATA[15:0]), .in1(MEM_READ_DATA[31:16]), .out(multiplexer_9_out), .sel(MEM_WRITE_ADDRESS[1]));
  Multiplexer #(.enable("false"), .width(8)) multiplexer_10 (
    .in0(multiplexer_7_out), .in1(multiplexer_8_out), .out(multiplexer_10_out), .sel(MEM_WRITE_ADDRESS[1]));
  assign bit_extender_1_out = {{16{multiplexer_9_out[15]}}, multiplexer_9_out};  // Bit_Extender bit_extender_1
  Comparator #(.mode("unsigned"), .width(3)) comparator_1 (
    .a(funct3), .b(3'b000), .eq(comparator_1_eq));  // open: gt, lt
  Comparator #(.mode("unsigned"), .width(3)) comparator_2 (
    .a(funct3), .b(3'b001), .eq(comparator_2_eq));  // open: gt, lt
  Comparator #(.mode("unsigned"), .width(3)) comparator_3 (
    .a(funct3), .b(3'b010), .eq(comparator_3_eq));  // open: gt, lt
  assign bit_extender_2_out = {{24{multiplexer_10_out[7]}}, multiplexer_10_out};  // Bit_Extender bit_extender_2
  not not_1 (not_1_out, MEM_WRITE_ADDRESS[0]);
  not not_2 (not_2_out, MEM_WRITE_ADDRESS[1]);
  Multiplexer #(.enable("false"), .width(32)) multiplexer_11 (
    .in0(bit_extender_2_out), .in1(bit_extender_1_out), .out(multiplexer_11_out), .sel(funct3[0]));
  and and_1 (and_1_out, comparator_1_eq, not_1_out, not_2_out);
  and and_2 (and_2_out, comparator_1_eq, MEM_WRITE_ADDRESS[0], not_2_out);
  and and_3 (and_3_out, comparator_1_eq, not_1_out, MEM_WRITE_ADDRESS[1]);
  and and_4 (and_4_out, comparator_1_eq, MEM_WRITE_ADDRESS[0], MEM_WRITE_ADDRESS[1]);
  and and_5 (and_5_out, comparator_2_eq, not_1_out, not_2_out);
  and and_6 (and_6_out, comparator_2_eq, not_1_out, MEM_WRITE_ADDRESS[1]);
  and and_7 (and_7_out, comparator_3_eq, not_1_out, not_2_out);
  Multiplexer #(.enable("false"), .width(32)) multiplexer_12 (
    .in0(multiplexer_11_out), .in1(MEM_READ_DATA), .out(read), .sel(funct3[1]));
  Priority_Encoder #(.select(4)) priority_encoder_1 (
    .in1(and_1_out), .in2(and_2_out), .in3(and_5_out), .in4(and_3_out), .in8(and_4_out), .in12(and_6_out),
    .in15(and_7_out), .out(priority_encoder_1_out), .en_in(control_logic_1_memrw));  // open: in0, in5, in6, in7, in9, in10, in11, in13, in14, gs, en_out
  Multiplexer #(.enable("false"), .width(4)) multiplexer_13 (
    .in0(4'b0000), .in1(priority_encoder_1_out), .out(MEM_WRITE_ENABLE), .sel(control_logic_1_memrw));
  Comparator #(.mode("unsigned"), .width(4)) comparator_4 (
    .a(4'b1111), .b(MEM_WRITE_ENABLE), .eq(comparator_4_eq));  // open: gt, lt
  Multiplexer #(.enable("false"), .width(32)) multiplexer_14 (
    .in0({32{1'b0}}),
    .in1({regfile_1_read_data_2_4, regfile_1_read_data_2_3, regfile_1_read_data_2_2, regfile_1_read_data_2}),
    .out(multiplexer_14_out), .sel(comparator_4_eq));
  Multiplexer #(.enable("false"), .width(8)) multiplexer_15 (
    .in0({8{1'b0}}), .in1(regfile_1_read_data_2), .out(multiplexer_15_out), .sel(MEM_WRITE_ENABLE[0]));
  Multiplexer #(.enable("false"), .width(8)) multiplexer_16 (
    .in0({8{1'b0}}), .in1(regfile_1_read_data_2), .out(multiplexer_16_out), .sel(MEM_WRITE_ENABLE[1]));
  Multiplexer #(.enable("false"), .width(8)) multiplexer_17 (
    .in0({8{1'b0}}), .in1(regfile_1_read_data_2), .out(multiplexer_17_out), .sel(MEM_WRITE_ENABLE[2]));
  Multiplexer #(.enable("false"), .width(8)) multiplexer_18 (
    .in0({8{1'b0}}), .in1(regfile_1_read_data_2), .out(multiplexer_18_out), .sel(MEM_WRITE_ENABLE[3]));
  Multiplexer #(.enable("false"), .width(8)) multiplexer_19 (
    .in0({8{1'b0}}), .in1(regfile_1_read_data_2), .out(multiplexer_19_out), .sel(MEM_WRITE_ENABLE[0]));
  Multiplexer #(.enable("false"), .width(8)) multiplexer_20 (
    .in0({8{1'b0}}), .in1(regfile_1_read_data_2_2), .out(multiplexer_20_out), .sel(MEM_WRITE_ENABLE[1]));
  Multiplexer #(.enable("false"), .width(8)) multiplexer_21 (
    .in0({8{1'b0}}), .in1(regfile_1_read_data_2), .out(multiplexer_21_out), .sel(MEM_WRITE_ENABLE[2]));
  Multiplexer #(.enable("false"), .width(8)) multiplexer_22 (
    .in0({8{1'b0}}), .in1(regfile_1_read_data_2_2), .out(multiplexer_22_out), .sel(MEM_WRITE_ENABLE[3]));
  Comparator #(.mode("unsigned"), .width(3)) comparator_5 (
    .a(funct3), .b(3'b000), .eq(comparator_5_eq));  // open: gt, lt
  Comparator #(.mode("unsigned"), .width(3)) comparator_6 (
    .a(funct3), .b(3'b001), .eq(comparator_6_eq));  // open: gt, lt
  Comparator #(.mode("unsigned"), .width(3)) comparator_7 (
    .a(funct3), .b(3'b010), .eq(comparator_7_eq));  // open: gt, lt
  Priority_Encoder #(.select(2)) priority_encoder_2 (
    .in0(comparator_5_eq), .in1(comparator_6_eq), .in2(comparator_7_eq), .out(priority_encoder_2_out));  // open: in3, gs, en_out, en_in
  Multiplexer #(.enable("false"), .select(2), .width(32)) multiplexer_23 (
    .in0({multiplexer_18_out, multiplexer_17_out, multiplexer_16_out, multiplexer_15_out}),
    .in1({multiplexer_22_out, multiplexer_21_out, multiplexer_20_out, multiplexer_19_out}),
    .in2(multiplexer_14_out), .out(MEM_WRITE_DATA), .sel(priority_encoder_2_out));  // open: in3

  // Other names for the same wires on the sheet: opcode[6:0] = ins[6:0]; rd[4:0] = ins[11:7];
  //   ins (some bits) = {csrr, funct3}; rs1[4:0] = ins[19:15]; rs2[4:0] = csrr[4:0]

  // Notes on the sheet:
  //   Output to IMEM
  //   IMEM (do **NOT** move this)
  //   Inputs from IMEM
  //   It is OK to move the PC, RegFile, ALU, MEM, Branch Comp, Imm Gen, and Control Logic to wherever is most convenient for you when constructing your CPU, and to delete this text
  //   Inputs/Outputs for testing. Do **NOT** move these.
  //   Outputs To DMEM
  //   DMEM (do **NOT** move this)
  //   Inputs From DMEM
endmodule
